# Fritzing sketch sample-plan (saved by Fritzing 0.9.5d)
breadboards: 1

parts:
  U1 = ESP 32 DEVKIT DOIT
  Componente1 = Bluetooth HC-05 Macho
  R1 = Resistor [tolerance=±5% resistance=220 package=THT]
  R2 = Resistor [tolerance=±5% resistance=220 package=THT]
  R4 = Resistor [tolerance=±5% resistance=220 package=THT]
  SG2 = Buzzer 12mm [package=buzzer-ccv-kit]
  LED1 = RGB LED (com. anode, rbg) [package="5 mm [THT]"]
  R5 = Resistor [tolerance=±5% resistance=220 package=THT]

nets:
  GND: U1.GND, Componente1.GND, SG2.2, LED1.red_cathode
  N1: R1.Pin_1, LED1.green_cathode
  N2: R2.Pin_1, LED1.blue_cathode
  N3: R4.Pin_1, LED1.common_anode
  N4: SG2.1, R5.Pin_1
